// Digital circuit ALU.dig as structural Verilog
module ALU (
  input  [7:0] A,
  input  [7:0] B,
  input  Do_Minus,
  output [7:0] Result,
  output NegFlag,
  output ZeroFlag,
  output OverflowFlag
);

  wire _8bits_adder_1_c_o, and_2_out, demultiplexer_4_out_0, not_3_out, not_4_out;
  wire [7:0] _8bits_adder_1_s, _8bits_adder_2_s, demultiplexer_1_out_0, demultiplexer_1_out_1,
       demultiplexer_2_out_0, demultiplexer_2_out_1, demultiplexer_3_out_0, demultiplexer_3_out_1,
       multiplexer_1_out, multiplexer_2_out, not_1_out, not_2_out;

  Demultiplexer #(.Bits(8)) demultiplexer_1 (
    .sel(Do_Minus), .in(B), .out_0(demultiplexer_1_out_0), .out_1(demultiplexer_1_out_1));
  assign not_1_out = ~demultiplexer_1_out_1;  // Not not_1, 8 bits wide
  Multiplexer #(.Bits(8)) multiplexer_1 (
    .sel(Do_Minus), .in_0(demultiplexer_1_out_0), .in_1(not_1_out), .out(multiplexer_1_out));
  _8bits_adder _8bits_adder_1 (.A(A), .B(multiplexer_1_out), .C(1'b0), .S(_8bits_adder_1_s), .C_o(_8bits_adder_1_c_o));
  Demultiplexer #(.Bits(8)) demultiplexer_2 (
    .sel(Do_Minus), .in(_8bits_adder_1_s), .out_0(demultiplexer_2_out_0), .out_1(demultiplexer_2_out_1));
  Demultiplexer #(.Bits(8)) demultiplexer_3 (
    .sel(_8bits_adder_1_c_o), .in(demultiplexer_2_out_1), .out_0(demultiplexer_3_out_0),
    .out_1(demultiplexer_3_out_1));
  assign not_2_out = ~demultiplexer_3_out_0;  // Not not_2, 8 bits wide
  not not_3 (not_3_out, Do_Minus);
  _8bits_adder _8bits_adder_2 (
    .A(demultiplexer_3_out_1), .B({8{1'b0}}), .C(_8bits_adder_1_c_o), .S(_8bits_adder_2_s));  // open: C_o
  and and_1 (OverflowFlag, _8bits_adder_1_c_o, not_3_out);
  Multiplexer #(.Bits(8)) multiplexer_2 (
    .sel(_8bits_adder_1_c_o), .in_0(not_2_out), .in_1(_8bits_adder_2_s), .out(multiplexer_2_out));
  Multiplexer #(.Bits(8)) multiplexer_3 (
    .sel(Do_Minus), .in_0(demultiplexer_2_out_0), .in_1(multiplexer_2_out), .out(Result));
  not not_4 (not_4_out, _8bits_adder_1_c_o);
  and and_2 (and_2_out, Do_Minus, not_4_out);
  nor nor_1 (ZeroFlag, Result[0], Result[1], Result[2], Result[3], Result[4], Result[5], Result[6], Result[7]);
  Demultiplexer demultiplexer_4 (.sel(ZeroFlag), .in(and_2_out), .out_0(demultiplexer_4_out_0));  // open: out_1
  Multiplexer multiplexer_4 (.sel(ZeroFlag), .in_0(demultiplexer_4_out_0), .in_1(1'b0), .out(NegFlag));
endmodule

/* Test case:
A	B	Do_Minus	OverflowFlag	NegFlag	ZeroFlag	Result
2	5	1		0		1	0		3
250	15	0		1		0	0		9
50	50	1		0		0	1		0
0	0	0		0		0	1		0
255	1	0		1		0	1		0
*/
