// Digital circuit forward_register.dig as structural Verilog
module forward_register (
  input  [7:0] Data_PostEX,
  input  [2:0] R_Dest_In,
  input  [1:0] Do_SMTH,
  input  CLK,
  input  [7:0] Data_1,
  input  [7:0] Data_2,
  input  [2:0] R_Src1,
  input  [2:0] R_Src2,
  input  IMM_Check,
  output [7:0] Out_1,
  output [7:0] Out_2
);

  wire and_1_out, and_2_out, comparator_1_eq, comparator_2_eq, comparator_3_eq, comparator_4_eq, xnor_1_out;
  wire [2:0] DataForward_Reg_1_q_2, DataForward_Reg_2_q_2;
  wire [7:0] DataForward_Reg_1_q, DataForward_Reg_2_q, multiplexer_2_out, multiplexer_3_out,
       multiplexer_4_out, multiplexer_5_out, multiplexer_6_out, multiplexer_7_out, multiplexer_9_out;
  wire [11:0] multiplexer_1_out;
  wire [11:11] DataForward_Reg_1_q_3, DataForward_Reg_2_q_3;

  xnor xnor_1 (xnor_1_out, Do_SMTH[0], Do_SMTH[1]);
  Multiplexer #(.Bits(12)) multiplexer_1 (
    .sel(xnor_1_out), .in_0({12{1'b0}}), .in_1({1'b1, R_Dest_In, Data_PostEX}), .out(multiplexer_1_out));
  Register #(.Bits(12)) DataForward_Reg_1 (
    .D(multiplexer_1_out), .C(CLK), .en(xnor_1_out),
    .Q({DataForward_Reg_1_q_3[11], DataForward_Reg_1_q_2, DataForward_Reg_1_q}));
  Register #(.Bits(12)) DataForward_Reg_2 (
    .D({DataForward_Reg_1_q_3[11], DataForward_Reg_1_q_2, DataForward_Reg_1_q}), .C(CLK), .en(xnor_1_out),
    .Q({DataForward_Reg_2_q_3[11], DataForward_Reg_2_q_2, DataForward_Reg_2_q}));
  Multiplexer #(.Bits(8)) multiplexer_2 (
    .sel(DataForward_Reg_1_q_3[11]), .in_0(Data_1), .in_1(DataForward_Reg_1_q), .out(multiplexer_2_out));
  Comparator #(.Bits(3)) comparator_1 (.a(DataForward_Reg_1_q_2), .b(R_Src1), .eq(comparator_1_eq));  // open: gt, lt
  Comparator #(.Bits(3)) comparator_2 (.a(DataForward_Reg_1_q_2), .b(R_Src2), .eq(comparator_2_eq));  // open: gt, lt
  Multiplexer #(.Bits(8)) multiplexer_3 (
    .sel(DataForward_Reg_2_q_3[11]), .in_0(Data_2), .in_1(DataForward_Reg_2_q), .out(multiplexer_3_out));
  Comparator #(.Bits(3)) comparator_3 (.a(DataForward_Reg_2_q_2), .b(R_Src1), .eq(comparator_3_eq));  // open: gt, lt
  Comparator #(.Bits(3)) comparator_4 (.a(DataForward_Reg_2_q_2), .b(R_Src2), .eq(comparator_4_eq));  // open: gt, lt
  Multiplexer #(.Bits(8)) multiplexer_4 (
    .sel(comparator_1_eq), .in_0(Data_1), .in_1(multiplexer_2_out), .out(multiplexer_4_out));
  Multiplexer #(.Bits(8)) multiplexer_5 (
    .sel(comparator_2_eq), .in_0(Data_2), .in_1(multiplexer_2_out), .out(multiplexer_5_out));
  Multiplexer #(.Bits(8)) multiplexer_6 (
    .sel(comparator_3_eq), .in_0(Data_1), .in_1(multiplexer_3_out), .out(multiplexer_6_out));
  Multiplexer #(.Bits(8)) multiplexer_7 (
    .sel(comparator_4_eq), .in_0(Data_2), .in_1(multiplexer_3_out), .out(multiplexer_7_out));
  and and_1 (and_1_out, comparator_1_eq, comparator_3_eq);
  and and_2 (and_2_out, comparator_2_eq, comparator_4_eq);
  Multiplexer #(.Bits(8)) multiplexer_8 (
    .sel(and_1_out), .in_0(multiplexer_6_out), .in_1(multiplexer_4_out), .out(Out_1));
  Multiplexer #(.Bits(8)) multiplexer_9 (
    .sel(and_2_out), .in_0(multiplexer_7_out), .in_1(multiplexer_5_out), .out(multiplexer_9_out));
  Multiplexer #(.Bits(8)) multiplexer_10 (.sel(IMM_Check), .in_0(multiplexer_9_out), .in_1(Data_2), .out(Out_2));
endmodule
